# Fritzing sketch Class_Quality_KYKLOMA (saved by Fritzing 0.9.3b)
breadboards: 1

parts:
  Part1 = Arduino Uno (Rev3)
  Part2 = Breakout Board for Electret Microphone
  Εξάρτημα1 = MQ-7 breakout  # not connected
  DHT1 = Humidity and Temperature Sensor DHT11
  Part3 = BH1750
  R1 = Resistor [tolerance=±5% resistance=10k package=THT]
  Part4 = KY-013 Analog Temperature Sensor Module [package="Breakout board"]
  Εξάρτημα2 = LCD Keypad Shield  # not connected

nets:
  N1: Part1.A2, Part2.VCC
  VCC: Part1.5V, Part2.AUD, DHT1.Vcc, Part3.VCC, Part4.S
  GND: Part1.GND, Part2.GND, DHT1.GND_2, Part3.GND, Part4.Vin
  N2: DHT1.Data-signal, R1.Pin_1

notes:
  ΤΡΟΦΟΔΟΣΙΑ GAS ΚΑΤΕΥΘΕΙΑΝ ΑΠΟ ΚΕΝΤΡΙΚΗ ΤΡΟΦΟΔΟΣΙΑ

custom parts:
  MQ-7 breakout: SKU: 101282
  Humidity and Temperature Sensor DHT11: Digital relative humidity & temperature sensor DHT11
  BH1750: Light Sensor
  KY-013 Analog Temperature Sensor Module: KY-013 Analog Temperature Sensor module, measures ambient temperature based on resistance of the thermistor.
  LCD Keypad Shield: It consists of a 1602 white character blue backlight LCD. The keypad consists of 5 keys — select, up, right, down and left. To save the digital IO pins, the keypad interface uses only one ADC channel. The key value is read through a 5 stage voltage divider.
