# Fritzing sketch competition 2 (saved by Fritzing 0.9.3b)
breadboards: 1

parts:
  Part1 = Arduino Uno (Rev3)
  Part2 = Breakout Board for Electret Microphone
  Εξάρτημα1 = MQ-7 breakout  # not connected
  DHT1 = Humidity and Temperature Sensor DHT11
  Part3 = BH1750
  R1 = Resistor [tolerance=±5% resistance=10k package=THT]
  Part4 = KY-013 Analog Temperature Sensor Module [package="Breakout board"]

nets:
  N1: Part1.A2, Part2.VCC
  5V: Part1.5V, Part2.AUD, DHT1.GND_1, Part3.VCC, Part4.S
  GND: Part1.GND, Part2.GND, DHT1.GND_2, Part3.GND, Part4.Vin
  N2: DHT1.Vcc, R1.Pin_0
  N3: DHT1.Data-signal, R1.Pin_1

custom parts:
  MQ-7 breakout: SKU: 101282
  Humidity and Temperature Sensor DHT11: Digital relative humidity & temperature sensor DHT11
  BH1750: Light Sensor
  KY-013 Analog Temperature Sensor Module: KY-013 Analog Temperature Sensor module, measures ambient temperature based on resistance of the thermistor.
